// Logisim project HW1of231Maybe.circ as structural Verilog: 1 circuit, main circuit main
module main (
  input  A,
  input  B,
  input  C
);

  wire nand_1_out, nand_2_out, nand_3_out, nand_4_out;

  nand nand_1 (nand_1_out, A, C);
  not nand_2 (nand_2_out, C);  // NAND_Gate
  nand nand_3 (nand_3_out, B, nand_2_out);
  nand nand_4 (nand_4_out, nand_1_out, nand_3_out);
  LED led_1 (.in(nand_4_out));

  // Notes on the sheet:
  //                ID: 2221458642
  //   Section: 14
  //   Name: Shadman Shahriar
  //   F(A,B,C) = AC+BC'
endmodule
