// Logisim project Lab231ProjectGeneralPOS.circ as structural Verilog: 1 circuit, main circuit main
module main (
  input  X,
  input  Y,
  input  Z
);

  wire A, B, C, D, E, F, G, not_1_out, not_2_out, not_3_out, or_1_out, or_2_out, or_3_out, or_4_out,
       or_6_out, or_7_out;

  not not_1 (not_1_out, X);
  not not_2 (not_2_out, Z);
  not not_3 (not_3_out, Y);
  or or_1 (or_1_out, X, not_3_out, Z);
  or or_2 (or_2_out, not_1_out, Y, Z);
  or or_3 (or_3_out, not_1_out, Y, not_2_out);
  or or_4 (or_4_out, not_1_out, not_3_out, not_2_out);
  or or_5 (G, X, Y, Z);
  or or_6 (or_6_out, X, Y, not_2_out);
  or or_7 (or_7_out, X, not_3_out, not_2_out);
  and and_1 (A, or_6_out, or_7_out);
  and and_2 (B, or_6_out, or_1_out, or_7_out, or_2_out, or_3_out, or_4_out);
  and and_3 (C, or_1_out, or_3_out);
  and and_4 (D, or_6_out, G, or_1_out);
  and and_5 (E, G, or_2_out);
  and and_6 (F, G, or_7_out);
  _7_Segment_Display u_7_segment_display_1 (.g(G), .f(F), .a(A), .b(B), .e(E), .d(D), .c(C));  // open: dp

  // Notes on the sheet:
  //   General POS format
endmodule
