// Logisim project LabProject231.circ as structural Verilog: 1 circuit, main circuit main
module main (
  input  X,
  input  Y,
  input  Z
);

  wire and_1_out, and_2_out, and_3_out, and_4_out, and_5_out, and_6_out, and_7_out, and_8_out, not_1_out,
       not_2_out, not_3_out, or_1_out, or_2_out, or_3_out, or_4_out, or_5_out, or_6_out, or_7_out;

  not not_1 (not_1_out, X);
  not not_2 (not_2_out, Y);
  not not_3 (not_3_out, Z);
  or or_1 (or_1_out, X, not_3_out);
  and and_1 (and_1_out, not_1_out, not_3_out, not_2_out);
  and and_2 (and_2_out, not_3_out, X, Y);
  and and_3 (and_3_out, not_2_out, not_3_out);
  and and_4 (and_4_out, not_1_out, Z);
  and and_5 (and_5_out, X, Y);
  and and_6 (and_6_out, Y, Z);
  or or_2 (or_2_out, Y, Z);
  or or_3 (or_3_out, and_6_out, X);
  or or_4 (or_4_out, X, Y, Z);
  or or_5 (or_5_out, and_1_out, and_2_out);
  or or_6 (or_6_out, and_3_out, and_4_out, and_5_out);
  and and_7 (and_7_out, not_2_out, Z);
  and and_8 (and_8_out, Y, not_3_out);
  or or_7 (or_7_out, and_7_out, X, and_8_out);
  _7_Segment_Display u_7_segment_display_1 (
    .g(or_4_out), .f(or_7_out), .a(or_1_out), .b(or_5_out), .e(or_2_out), .d(or_3_out), .c(or_6_out));  // open: dp

  // Notes on the sheet:
  //   SOP circuit for Lab Project
endmodule
