// Logisim project LabProject231GenSOP.circ as structural Verilog: 1 circuit, main circuit main
module main (
  input  X,
  input  Y,
  input  Z
);

  wire A, and_1_out, and_2_out, and_3_out, and_4_out, and_5_out, and_6_out, and_7_out, and_8_out, B, C, D, E,
       F, G, not_1_out, not_2_out, not_3_out;

  not not_1 (not_1_out, X);
  not not_2 (not_2_out, Y);
  not not_3 (not_3_out, Z);
  and and_1 (and_1_out, not_1_out, not_2_out, Z);
  and and_2 (and_2_out, not_1_out, Y, Z);
  and and_3 (and_3_out, not_1_out, not_2_out, not_3_out);
  and and_4 (and_4_out, not_1_out, Y, not_3_out);
  and and_5 (and_5_out, X, not_2_out, not_3_out);
  and and_6 (and_6_out, X, not_2_out, Z);
  and and_7 (and_7_out, X, Y, not_3_out);
  and and_8 (and_8_out, X, Y, Z);
  or or_1 (A, and_3_out, and_4_out, and_5_out, and_6_out, and_7_out, and_8_out);
  or or_2 (B, and_3_out, and_7_out);
  or or_3 (C, and_3_out, and_1_out, and_2_out, and_5_out, and_7_out, and_8_out);
  or or_4 (D, and_2_out, and_5_out, and_6_out, and_7_out, and_8_out);
  or or_5 (E, and_1_out, and_4_out, and_2_out, and_7_out, and_6_out, and_8_out);
  or or_6 (F, and_1_out, and_4_out, and_5_out, and_6_out, and_7_out, and_8_out);
  or or_7 (G, and_1_out, and_4_out, and_5_out, and_2_out, and_6_out, and_7_out, and_8_out);
  _7_Segment_Display u_7_segment_display_1 (.g(G), .f(F), .a(A), .b(B), .e(E), .d(D), .c(C));  // open: dp

  // Notes on the sheet:
  //   Generalised SOP circuit
endmodule
