// Logisim project LabProject231NANDSimplified.circ as structural Verilog: 1 circuit, main circuit main
module main (
  input  X,
  input  Y,
  input  Z
);

  wire A, B, C, D, E, F, G, nand_1_out, nand_2_out, nand_3_out, nand_5_out, nand_6_out, nand_7_out,
       nand_8_out, nand_9_out, nand_10_out, nand_11_out, nand_12_out, nand_14_out, nand_15_out, nand_16_out,
       nand_18_out;

  nand nand_1 (nand_1_out, Y, Y);
  nand nand_2 (nand_2_out, X, X);
  nand nand_3 (nand_3_out, Z, Z);
  nand nand_4 (A, nand_2_out, Z);
  nand nand_5 (nand_5_out, X, nand_1_out);
  nand nand_6 (nand_6_out, nand_2_out, Y);
  nand nand_7 (nand_7_out, nand_2_out, Y, nand_3_out);
  nand nand_8 (nand_8_out, X, nand_1_out, Z);
  nand nand_9 (nand_9_out, nand_2_out, nand_1_out);
  nand nand_10 (nand_10_out, nand_2_out, nand_3_out);
  nand nand_11 (nand_11_out, nand_2_out, nand_1_out, nand_3_out);
  nand nand_12 (nand_12_out, nand_2_out, Y, Z);
  nand nand_13 (G, nand_2_out, nand_1_out, nand_3_out);
  nand nand_14 (nand_14_out, nand_5_out, nand_6_out, nand_3_out);
  nand nand_15 (nand_15_out, nand_7_out, nand_8_out);
  nand nand_16 (nand_16_out, nand_9_out, nand_10_out);
  nand nand_17 (E, nand_1_out, nand_3_out);
  nand nand_18 (nand_18_out, nand_11_out, nand_12_out);
  nand nand_19 (B, nand_14_out, nand_14_out);
  nand nand_20 (C, nand_15_out, nand_15_out);
  nand nand_21 (D, nand_16_out, nand_16_out);
  nand nand_22 (F, nand_18_out, nand_18_out);
  _7_Segment_Display u_7_segment_display_1 (.g(G), .f(F), .a(A), .b(B), .e(E), .d(D), .c(C));  // open: dp

  // Notes on the sheet:
  //   NAND simplification(POS)
endmodule
