// Logisim project LabProject231SimplifiedPOS.circ as structural Verilog: 1 circuit, main circuit main
module main (
  input  X,
  input  Y,
  input  Z
);

  wire A, B, C, D, E, F, G, not_1_out, not_2_out, not_3_out, or_2_out, or_3_out, or_4_out, or_5_out,
       or_6_out, or_7_out, or_10_out;

  not not_1 (not_1_out, X);
  not not_2 (not_2_out, Y);
  not not_3 (not_3_out, Z);
  or or_1 (A, X, not_3_out);
  or or_2 (or_2_out, X, not_2_out);
  or or_3 (or_3_out, not_1_out, Y);
  or or_4 (or_4_out, X, not_2_out, Z);
  or or_5 (or_5_out, not_1_out, Y, not_3_out);
  or or_6 (or_6_out, X, Y);
  or or_7 (or_7_out, X, Z);
  or or_8 (E, Y, Z);
  or or_9 (G, X, Y, Z);
  or or_10 (or_10_out, X, not_2_out, not_3_out);
  and and_1 (C, or_4_out, or_5_out);
  and and_2 (D, or_6_out, or_7_out);
  and and_3 (F, G, or_10_out);
  and and_4 (B, or_2_out, not_3_out, or_3_out);
  _7_Segment_Display u_7_segment_display_1 (.g(G), .f(F), .a(A), .b(B), .e(E), .d(D), .c(C));  // open: dp

  // Notes on the sheet:
  //   Simplified POS circuit
endmodule
