// Logisim project NORGateSimpCircuit.circ as structural Verilog: 1 circuit, main circuit main
module main (
  input  X,
  input  Y,
  input  Z
);

  wire A, B, C, D, E, F, G, nor_1_out, nor_2_out, nor_3_out, nor_4_out, nor_5_out, nor_6_out, nor_7_out,
       nor_8_out, nor_9_out, nor_10_out, nor_11_out, nor_12_out, nor_13_out;

  nor nor_1 (nor_1_out, X, X);
  nor nor_2 (nor_2_out, Y, Y);
  nor nor_3 (nor_3_out, Z, Z);
  nor nor_4 (nor_4_out, X, nor_3_out);
  nor nor_5 (nor_5_out, nor_1_out, Y);
  nor nor_6 (nor_6_out, X, nor_2_out);
  nor nor_7 (nor_7_out, X, nor_2_out, Z);
  nor nor_8 (nor_8_out, nor_1_out, Y, nor_3_out);
  nor nor_9 (nor_9_out, X, Y);
  nor nor_10 (nor_10_out, X, Z);
  nor nor_11 (nor_11_out, Y, Z);
  nor nor_12 (nor_12_out, X, Y, Z);
  nor nor_13 (nor_13_out, X, nor_2_out, nor_3_out);
  nor nor_14 (A, nor_4_out, nor_4_out);
  nor nor_15 (B, nor_5_out, nor_6_out, Z);
  nor nor_16 (C, nor_7_out, nor_8_out);
  nor nor_17 (D, nor_9_out, nor_10_out);
  nor nor_18 (E, nor_11_out, nor_11_out);
  nor nor_19 (F, nor_12_out, nor_13_out);
  not nor_20 (G, nor_12_out);  // NOR_Gate
  _7_Segment_Display u_7_segment_display_1 (.g(G), .f(F), .a(A), .b(B), .e(E), .d(D), .c(C));  // open: dp

  // Notes on the sheet:
  //   NOR gate simplified circuit(POS)
endmodule
