// Logisim project potentialCircuitHW.circ as structural Verilog: 1 circuit, main circuit main
module main (
  input  A,
  input  B,
  input  C
);

  wire nor_1_out, nor_2_out, nor_3_out, nor_4_out, nor_5_out, nor_6_out, nor_7_out;

  nor nor_1 (nor_1_out, A, A);
  nor nor_2 (nor_2_out, C, C);
  nor nor_3 (nor_3_out, B, B);
  nor nor_4 (nor_4_out, nor_1_out, nor_2_out);
  nor nor_5 (nor_5_out, C, nor_3_out);
  nor nor_6 (nor_6_out, nor_4_out, nor_5_out);
  LED led_1 (.in(nor_7_out));
  nor nor_7 (nor_7_out, nor_6_out, nor_6_out);
endmodule
